# Fritzing sketch Final_Project_Group1 (saved by Fritzing 0.9.9b)
breadboards: 1

parts:
  J1 = STM32 Nucleo boards
  ZS-042_RTC1 = ZS-042 RTC Module
  M2 = SparkFun Pulse Oximeter Heart-Rate Sensor [package=THT]
  Mod1 = KY-028 Digital Temperature Sensor Module [package="Breakout board"]
  OLED_I2C1 = OLED 128x64 I2C Monochrome Display
  LED1 = smd LED [color="Red (633nm)" package="1206 [SMD]"]
  R1 = Resistor [tolerance=±5% power=0.25 resistance=220 package=THT]
  Mod2 = Passive Buzzer

nets:
  N1: J1.A0, Mod1.A0
  N2: J1.A4/SDA, M2.!MFIO
  N3: J1.A5/SCL, M2.!RST
  N4: J1.D8, Mod2.S
  N5: J1.D10_PWM/SS, ZS-042_RTC1.SCL, M2.SCL, M2.SCL-Qwiic2, OLED_I2C1.SCK
  N6: J1.D7, R1.Pin_0
  3V3: J1.3V3, J1.PB7, ZS-042_RTC1.VCC, ZS-042_RTC1.SDA, M2.SDA, M2.3.3V, M2.3.3V-Qwiic1, M2.SDA-Qwiic2, Mod1.+, OLED_I2C1.SDA, OLED_I2C1.VDD
  GND: J1.GND, ZS-042_RTC1.GND, M2.GND, Mod1.G, OLED_I2C1.GND, LED1.anode, Mod2.-
  N7: LED1.cathode, R1.Pin_1

custom parts:
  SparkFun Pulse Oximeter Heart-Rate Sensor: .The SparkFun Pulse Oximeter and Heart Rate Sensor is an I2C based biometric sensor, utilizing two chips from Maxim Integrated: the MAX32664 Biometric Sensor Hub and the MAX30101 Pulse Oximetry and Heart Rate Module. While the latter does all the sensing, the former is an incredibly small and fast Cortex M4 processor that handles all of the algorithmic calculations, digital filtering,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
  KY-028 Digital Temperature Sensor Module: KY-028 Digital Temperature Sensor Module, used to measure changes in temperature.
